# Fritzing sketch buzzer (saved by Fritzing 1.0.5)
breadboards: 1

parts:
  Part1 = Arduino Uno (Rev3)
  S1 = Pushbutton [package="[THT]"]
  SP1 = SPEAKER [package=pcb_mount_speaker]

nets:
  N1: Part1.D8, SP1.-
  N2: Part1.D7, S1.Pin_3, S1.Pin_4
  N3: Part1.GND, S1.Pin_1, S1.Pin_2, SP1.+
